# Fritzing sketch Lights (saved by Fritzing 0.9.3b)
breadboards: 2

parts:
  part = RELAY-SOLIDSTATE [part_number=AM1S-0505SZ package=relay-s108t02]
  Part1 = Arduino Nano (Rev3.0) (ICSP)
  U3 = AD8210 - High Voltage Birdirectional Current Shunt Monitor [part_number=ADuM1201CR]
  J1 = Screw terminal - 2 pins [package=THT]  # not connected
  J3 = screw terminal, 4 pins  # not connected
  J2 = male pin header, 4 pins [form="♂ (male)"]
  J4 = male pin header, 4 pins [form="♂ (male)"]  # not connected
  J5 = male pin header, 4 pins [form="♂ (male)"]  # not connected
  U4 = AD8210 - High Voltage Birdirectional Current Shunt Monitor [part_number=ADuM1201CR]
  U5 = RS485 [package=so08]
  J6 = male pin header, 5 pins [form="♂ (male)"]
  J7 = male pin header, 3 pins [form="♂ (male)"]
  J8 = Screw terminal - 2 pins [package=THT]  # not connected
  J9 = screw terminal, 4 pins  # not connected

nets:
  N1: part.T1, Part1.GND, U3.NC, U4.NC, J6.pin5
  N2: part.T2, Part1.VIN, U3.-IN, U4.-IN
  N3: part.+, U3.OUT, J2.pin1, U4.OUT
  N4: part.-, U3.+IN, J2.pin2, U4.+IN
  N5: Part1.D2, U4.VREF2
  N6: Part1.D3, U3.VREF2
  N7: Part1.D6, U5.DI, J6.pin1
  N8: Part1.D8, U5.RO, J6.pin4
  N9: Part1.D9, U5._RE, J6.pin3
  N10: Part1.5V, U5.DE, J6.pin2
  N11: U3.V+, J2.pin3
  N12: J2.pin4, U4.V+
  N13: U5.GND, J7.pin1
  N14: U5.A, J7.pin2
  N15: U5.B, J7.pin3

notes:
  GND VCC DIN CIN
  GND TX RX VCC EN
  B A GND
  LED DRIVER BLOCK
